# Fritzing sketch Schematics (saved by Fritzing 0.9.3b)

parts:
  Part1 = Arduino Nano (Rev3.0)
  S1 = Square Pushbutton
  J1 = Basic Servo  # not connected
  L298N1 = L298N DC motor driver
  M1 = DC Motor  # not connected
  M2 = DC Motor  # not connected
  Part2 = Bluetooth HC-05 Macho
  VCC1 = Battery block 9V

nets:
  N1: Part1.D1/TX, Part2.RXD
  N2: Part1.D0/RX, Part2.TXD
  GND: Part1.GND, L298N1.GND, Part2.GND
  N3: Part1.D5, L298N1.IN1
  N4: Part1.D6, L298N1.IN2
  N5: Part1.D7, L298N1.IN3
  N6: Part1.D8, L298N1.IN4
  VIN: Part1.VIN, L298N1.5V
  3V3: Part1.3V3, Part2.VCC
  N7: S1.leg0, L298N1.12V
  N8: S1.leg1, VCC1.+

custom parts:
  L298N DC motor driver: 2x DC motor driver with 78M05 positive voltage regulator (7..35 V) L298N: max 46 V, 2 A Set 5 V Enable jumper to enable 5 V regultor (needed for the L298N) and +5 V output at screw terminal or supply external +5 V at screw terminal Set ENA and/or ENB to +5 V to enable motor permanently or supply ENA and/or ENB with PWM signal IN1 and IN2 set rotation directory for motor A (OUT1/OUT2) IN2 and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
